// Logisim project 1.FlipFlopD.circ as structural Verilog: 1 circuit, main circuit main
module main (
  input  D,
  output out_2,
  output out_3
);

  wire clock_1_out, nand_1_out, nand_2_out, nand_3_out, nand_4_out, nand_5_out, nand_6_out, not_1_out,
       not_2_out;

  not not_1 (not_1_out, D);
  Clock clock_1 (.out(clock_1_out));
  nand nand_1 (nand_1_out, out_3, D, clock_1_out);
  nand nand_2 (nand_2_out, clock_1_out, not_1_out, out_2);
  nand nand_3 (nand_3_out, nand_1_out, nand_4_out);
  nand nand_4 (nand_4_out, nand_3_out, nand_2_out);
  not not_2 (not_2_out, clock_1_out);
  nand nand_5 (nand_5_out, nand_3_out, not_2_out);
  nand nand_6 (nand_6_out, not_2_out, nand_4_out);
  nand nand_7 (out_2, nand_5_out, out_3);
  nand nand_8 (out_3, out_2, nand_6_out);
endmodule
