// Logisim project 1.FlipFlopJK.circ as structural Verilog: 1 circuit, main circuit main
module main (
  input  J,
  input  K,
  output q,
  output q_prime
);

  wire Cock_out, nand_1_out, nand_2_out, nand_3_out, nand_4_out, nand_5_out, nand_6_out, not_1_out;

  Clock Cock (.out(Cock_out));
  nand nand_1 (nand_1_out, q_prime, J, Cock_out);
  nand nand_2 (nand_2_out, Cock_out, K, q);
  nand nand_3 (nand_3_out, nand_1_out, nand_4_out);
  nand nand_4 (nand_4_out, nand_3_out, nand_2_out);
  not not_1 (not_1_out, Cock_out);
  nand nand_5 (nand_5_out, nand_3_out, not_1_out);
  nand nand_6 (nand_6_out, not_1_out, nand_4_out);
  nand nand_7 (q, nand_5_out, q_prime);
  nand nand_8 (q_prime, q, nand_6_out);
endmodule
