// Logisim project 10.Ula8Bits.circ as structural Verilog: 12 circuits, main circuit main
module main (
  input  [7:0] A,
  input  [7:0] B,
  input  [2:0] mult1,
  input  in_4,
  output [7:0] Saida,
  output out_6,
  output out_7
);

  wire [7:0] and_1_out, nand_1_out, nor_1_out, not_1_out, or_1_out, shift2dir_1_saida, shift2esq_1_saida,
       somadorfinal_1_saida, subtrator8bits_1_saida, xor_1_out;

  assign nand_1_out = ~(A & B);  // NAND_Gate nand_1, 8 bits wide
  assign and_1_out = A & B;  // AND_Gate and_1, 8 bits wide
  assign nor_1_out = ~(A | B);  // NOR_Gate nor_1, 8 bits wide
  assign xor_1_out = A ^ B;  // XOR_Gate xor_1, 8 bits wide
  assign or_1_out = A | B;  // OR_Gate or_1, 8 bits wide
  assign not_1_out = ~A;  // NOT_Gate not_1, 8 bits wide
  somadorfinal somadorfinal_1 (.A(A), .B(B), .Cout(out_6), .Saida(somadorfinal_1_saida));
  subtrator8bits subtrator8bits_1 (.Minuendo(A), .Subtraendo(B), .Sinal(out_7), .Saida(subtrator8bits_1_saida));
  shift2esq shift2esq_1 (.entrada(A), .saida(shift2esq_1_saida));
  shift2dir shift2dir_1 (.entrada(A), .saida(shift2dir_1_saida));
  mult16ent8bit mult16ent8bit_1 (
    .I0(nand_1_out), .I1(and_1_out), .I2(nor_1_out), .I3(xor_1_out), .I4(or_1_out), .I5(not_1_out),
    .I6(somadorfinal_1_saida), .I7(subtrator8bits_1_saida), .I8(shift2esq_1_saida), .I9(shift2dir_1_saida),
    .Multiplexador(mult1), .sel(in_4), .Saida(Saida));  // open: I10, I11, I12, I13, I14, II15

  // Notes on the sheet:
  //   nand
  //   and
  //   nor
  //   xor
  //   or 
  //   not
  //   I0/I8 = 000
  //   I1/I9 = 001
  //   I2/I10 = 010
  //   I3/I11 = 011
  //   I4/I12 = 100
  //   I5/I13 = 101
  //   I6/I14 = 110
  //   I7/I15 = 111
  //   intervalo I0-I7 (Chave Sel = 0)
  //   intervalo I8-I15 (Chave Sel = 1)
endmodule

module multiplexador8entradas (
  input  [2:0] sel,
  input  a,
  input  b,
  input  c,
  input  d,
  input  e,
  input  f,
  input  g,
  input  h,
  output saida
);

  wire and_1_out, and_2_out, and_3_out, and_4_out, and_5_out, and_6_out, and_7_out, and_8_out, not_1_out,
       not_2_out, not_3_out;

  not not_1 (not_1_out, sel[2]);
  not not_2 (not_2_out, sel[1]);
  not not_3 (not_3_out, sel[0]);
  and and_1 (and_1_out, a, not_1_out, not_2_out, not_3_out);
  and and_2 (and_2_out, b, not_1_out, not_2_out, sel[0]);
  and and_3 (and_3_out, c, not_1_out, sel[1], not_3_out);
  and and_4 (and_4_out, d, not_1_out, sel[1], sel[0]);
  and and_5 (and_5_out, e, sel[2], not_2_out, not_3_out);
  and and_6 (and_6_out, f, sel[2], not_2_out, sel[0]);
  and and_7 (and_7_out, g, sel[2], sel[1], not_3_out);
  and and_8 (and_8_out, h, sel[2], sel[1], sel[0]);
  or or_1 (saida, and_1_out, and_2_out, and_3_out, and_4_out, and_5_out, and_6_out, and_7_out, and_8_out);
endmodule

module somador1bit (
  input  a0,
  input  a1,
  input  cin,
  output s,
  output cout
);

  wire and_1_out, and_2_out, and_3_out, xor_1_out;

  xor xor_1 (xor_1_out, a0, a1);
  and and_1 (and_1_out, a0, a1);
  and and_2 (and_2_out, a1, cin);
  and and_3 (and_3_out, a0, cin);
  xor xor_2 (s, xor_1_out, cin);
  or or_1 (cout, and_1_out, and_2_out, and_3_out);
endmodule

module somador4bits (
  input  carryin,
  input  in_2,
  input  in_3,
  input  in_4,
  input  in_5,
  input  in_6,
  input  in_7,
  input  in_8,
  input  in_9,
  output c3,
  output c2,
  output c1,
  output c0,
  output cout_Overflow_ed7af212
);

  wire somador1bit_2_cout, somador1bit_3_cout, somador1bit_4_cout;

  somador1bit somador1bit_1 (.a1(in_6), .cin(somador1bit_2_cout), .a0(in_2), .s(c3), .cout(cout_Overflow_ed7af212));
  somador1bit somador1bit_2 (.a1(in_7), .cin(somador1bit_3_cout), .a0(in_3), .s(c2), .cout(somador1bit_2_cout));
  somador1bit somador1bit_3 (.a1(in_8), .cin(somador1bit_4_cout), .a0(in_4), .s(c1), .cout(somador1bit_3_cout));
  somador1bit somador1bit_4 (.a1(in_9), .cin(carryin), .a0(in_5), .s(c0), .cout(somador1bit_4_cout));
endmodule

module somador8bits (
  input  in_1,
  input  in_2,
  input  in_3,
  input  in_4,
  input  in_5,
  input  in_6,
  input  in_7,
  input  in_8,
  input  in_9,
  input  in_10,
  input  in_11,
  input  in_12,
  input  in_13,
  input  in_14,
  input  in_15,
  input  in_16,
  input  in_17,
  output out_18,
  output out_19,
  output out_20,
  output Resultado,
  output out_22,
  output out_23,
  output out_24,
  output out_25,
  output Overflow
);

  wire somador4bits_1_cout_overflow_ed7af212;

  somador4bits somador4bits_1 (
    .in_6(in_16), .in_2(in_14), .in_7(in_12), .in_3(in_10), .in_8(in_8), .in_4(in_6), .carryin(in_1),
    .in_9(in_4), .in_5(in_2), .cout_Overflow_ed7af212(somador4bits_1_cout_overflow_ed7af212), .c3(out_22),
    .c2(out_23), .c1(out_24), .c0(out_25));
  somador4bits somador4bits_2 (
    .in_6(in_17), .in_2(in_15), .in_7(in_13), .in_3(in_11), .in_8(in_9), .in_4(in_7),
    .carryin(somador4bits_1_cout_overflow_ed7af212), .in_9(in_5), .in_5(in_3),
    .cout_Overflow_ed7af212(Overflow), .c3(out_18), .c2(out_19), .c1(out_20), .c0(Resultado));
endmodule

module somadorfinal (
  input  [7:0] A,
  input  [7:0] B,
  output Cout,
  output [7:0] Saida
);

  somador8bits somador8bits_1 (
    .in_4(B[0]), .in_6(A[1]), .in_8(B[1]), .in_10(A[2]), .in_12(B[2]), .in_14(A[3]), .in_16(B[3]),
    .in_2(A[0]), .in_1(1'b0), .in_5(B[4]), .in_7(A[5]), .in_9(B[5]), .in_11(A[6]), .in_13(B[6]),
    .in_15(A[7]), .in_17(B[7]), .in_3(A[4]), .out_18(Saida[7]), .out_19(Saida[6]), .out_20(Saida[5]),
    .Resultado(Saida[4]), .out_22(Saida[3]), .out_23(Saida[2]), .out_24(Saida[1]), .out_25(Saida[0]),
    .Overflow(Cout));

  // Notes on the sheet:
  //   Overflow?
endmodule

module subtrator8bits (
  input  [7:0] Minuendo,
  input  [7:0] Subtraendo,
  output Sinal,
  output [7:0] Saida
);

  wire not_1_out, not_2_out, not_3_out, not_4_out, not_5_out, not_6_out, not_7_out, not_8_out;

  not not_1 (not_1_out, Subtraendo[0]);
  not not_2 (not_2_out, Subtraendo[1]);
  not not_3 (not_3_out, Subtraendo[2]);
  not not_4 (not_4_out, Subtraendo[3]);
  not not_5 (not_5_out, Subtraendo[4]);
  not not_6 (not_6_out, Subtraendo[5]);
  not not_7 (not_7_out, Subtraendo[6]);
  not not_8 (not_8_out, Subtraendo[7]);
  somador8bits somador8bits_1 (
    .in_4(not_1_out), .in_6(Minuendo[1]), .in_8(not_2_out), .in_10(Minuendo[2]), .in_12(not_3_out),
    .in_14(Minuendo[3]), .in_16(not_4_out), .in_2(Minuendo[0]), .in_1(1'b1), .in_5(not_5_out),
    .in_7(Minuendo[5]), .in_9(not_6_out), .in_11(Minuendo[6]), .in_13(not_7_out), .in_15(Minuendo[7]),
    .in_17(not_8_out), .in_3(Minuendo[4]), .out_18(Saida[7]), .out_19(Saida[6]), .out_20(Saida[5]),
    .Resultado(Saida[4]), .out_22(Saida[3]), .out_23(Saida[2]), .out_24(Saida[1]), .out_25(Saida[0]),
    .Overflow(Sinal));

  // Notes on the sheet:
  //   Overflow?
endmodule

module multiplexador2entradas (
  input  A,
  input  B,
  input  Sel,
  output out_4
);

  wire and_1_out, and_2_out, not_1_out;

  not not_1 (not_1_out, Sel);
  and and_1 (and_1_out, A, not_1_out);
  and and_2 (and_2_out, B, Sel);
  or or_1 (out_4, and_1_out, and_2_out);
endmodule

module multiplexador2pra1 (
  input  a7,
  input  b7,
  input  a6,
  input  b6,
  input  a5,
  input  b5,
  input  a4,
  input  b4,
  input  a3,
  input  b3,
  input  a2,
  input  b2,
  input  a1,
  input  b1,
  input  sel,
  input  a0,
  input  b0,
  output [7:0] Saida
);

  multiplexador2entradas multiplexador2entradas_1 (.A(a0), .B(b0), .Sel(sel), .out_4(Saida[0]));
  multiplexador2entradas multiplexador2entradas_2 (.A(a1), .B(b1), .Sel(sel), .out_4(Saida[1]));
  multiplexador2entradas multiplexador2entradas_3 (.A(a2), .B(b2), .Sel(sel), .out_4(Saida[2]));
  multiplexador2entradas multiplexador2entradas_4 (.A(a3), .B(b3), .Sel(sel), .out_4(Saida[3]));
  multiplexador2entradas multiplexador2entradas_5 (.A(a4), .B(b4), .Sel(sel), .out_4(Saida[4]));
  multiplexador2entradas multiplexador2entradas_6 (.A(a5), .B(b5), .Sel(sel), .out_4(Saida[5]));
  multiplexador2entradas multiplexador2entradas_7 (.A(a6), .B(b6), .Sel(sel), .out_4(Saida[6]));
  multiplexador2entradas multiplexador2entradas_8 (.A(a7), .B(b7), .Sel(sel), .out_4(Saida[7]));
endmodule

module mult16ent8bit (
  input  [7:0] I0,
  input  [7:0] I1,
  input  [7:0] I2,
  input  [7:0] I3,
  input  [7:0] I4,
  input  [7:0] I5,
  input  [7:0] I6,
  input  [7:0] I7,
  input  [7:0] I8,
  input  [7:0] I9,
  input  [7:0] I10,
  input  [7:0] I11,
  input  [7:0] I12,
  input  [7:0] I13,
  input  [7:0] I14,
  input  [7:0] II15,
  input  [2:0] Multiplexador,
  input  sel,
  output [7:0] Saida
);

  wire multiplexador8entradas_1_saida, multiplexador8entradas_2_saida, multiplexador8entradas_3_saida,
       multiplexador8entradas_4_saida, multiplexador8entradas_5_saida, multiplexador8entradas_6_saida,
       multiplexador8entradas_7_saida, multiplexador8entradas_8_saida, multiplexador8entradas_9_saida,
       multiplexador8entradas_10_saida, multiplexador8entradas_11_saida, multiplexador8entradas_12_saida,
       multiplexador8entradas_13_saida, multiplexador8entradas_14_saida, multiplexador8entradas_15_saida,
       multiplexador8entradas_16_saida;

  multiplexador8entradas multiplexador8entradas_1 (
    .sel(Multiplexador), .a(I0[0]), .b(I1[0]), .c(I2[0]), .d(I3[0]), .e(I4[0]), .f(I5[0]), .g(I6[0]),
    .h(I7[0]), .saida(multiplexador8entradas_1_saida));
  multiplexador8entradas multiplexador8entradas_2 (
    .sel(Multiplexador), .a(I0[1]), .b(I1[1]), .c(I2[1]), .d(I3[1]), .e(I4[1]), .f(I5[1]), .g(I6[1]),
    .h(I7[1]), .saida(multiplexador8entradas_2_saida));
  multiplexador8entradas multiplexador8entradas_3 (
    .sel(Multiplexador), .a(I0[2]), .b(I1[2]), .c(I2[2]), .d(I3[2]), .e(I4[2]), .f(I5[2]), .g(I6[2]),
    .h(I7[2]), .saida(multiplexador8entradas_3_saida));
  multiplexador8entradas multiplexador8entradas_4 (
    .sel(Multiplexador), .a(I0[3]), .b(I1[3]), .c(I2[3]), .d(I3[3]), .e(I4[3]), .f(I5[3]), .g(I6[3]),
    .h(I7[3]), .saida(multiplexador8entradas_4_saida));
  multiplexador8entradas multiplexador8entradas_5 (
    .sel(Multiplexador), .a(I0[4]), .b(I1[4]), .c(I2[4]), .d(I3[4]), .e(I4[4]), .f(I5[4]), .g(I6[4]),
    .h(I7[4]), .saida(multiplexador8entradas_5_saida));
  multiplexador8entradas multiplexador8entradas_6 (
    .sel(Multiplexador), .a(I0[5]), .b(I1[5]), .c(I2[5]), .d(I3[5]), .e(I4[5]), .f(I5[5]), .g(I6[5]),
    .h(I7[5]), .saida(multiplexador8entradas_6_saida));
  multiplexador8entradas multiplexador8entradas_7 (
    .sel(Multiplexador), .a(I0[6]), .b(I1[6]), .c(I2[6]), .d(I3[6]), .e(I4[6]), .f(I5[6]), .g(I6[6]),
    .h(I7[6]), .saida(multiplexador8entradas_7_saida));
  multiplexador8entradas multiplexador8entradas_8 (
    .sel(Multiplexador), .a(I0[7]), .b(I1[7]), .c(I2[7]), .d(I3[7]), .e(I4[7]), .f(I5[7]), .g(I6[7]),
    .h(I7[7]), .saida(multiplexador8entradas_8_saida));
  multiplexador2pra1 multiplexador2pra1_1 (
    .sel(sel), .a7(multiplexador8entradas_8_saida), .a6(multiplexador8entradas_7_saida),
    .a5(multiplexador8entradas_6_saida), .a4(multiplexador8entradas_5_saida),
    .a3(multiplexador8entradas_4_saida), .a2(multiplexador8entradas_3_saida),
    .a1(multiplexador8entradas_2_saida), .a0(multiplexador8entradas_1_saida),
    .b7(multiplexador8entradas_16_saida), .b6(multiplexador8entradas_15_saida),
    .b5(multiplexador8entradas_14_saida), .b4(multiplexador8entradas_13_saida),
    .b3(multiplexador8entradas_12_saida), .b2(multiplexador8entradas_11_saida),
    .b1(multiplexador8entradas_10_saida), .b0(multiplexador8entradas_9_saida), .Saida(Saida));
  multiplexador8entradas multiplexador8entradas_9 (
    .sel(Multiplexador), .a(I8[0]), .b(I9[0]), .c(I10[0]), .d(I11[0]), .e(I12[0]), .f(I13[0]), .g(I14[0]),
    .h(II15[0]), .saida(multiplexador8entradas_9_saida));
  multiplexador8entradas multiplexador8entradas_10 (
    .sel(Multiplexador), .a(I8[1]), .b(I9[1]), .c(I10[1]), .d(I11[1]), .e(I12[1]), .f(I13[1]), .g(I14[1]),
    .h(II15[1]), .saida(multiplexador8entradas_10_saida));
  multiplexador8entradas multiplexador8entradas_11 (
    .sel(Multiplexador), .a(I8[2]), .b(I9[2]), .c(I10[2]), .d(I11[2]), .e(I12[2]), .f(I13[2]), .g(I14[2]),
    .h(II15[2]), .saida(multiplexador8entradas_11_saida));
  multiplexador8entradas multiplexador8entradas_12 (
    .sel(Multiplexador), .a(I8[3]), .b(I9[3]), .c(I10[3]), .d(I11[3]), .e(I12[3]), .f(I13[3]), .g(I14[3]),
    .h(II15[3]), .saida(multiplexador8entradas_12_saida));
  multiplexador8entradas multiplexador8entradas_13 (
    .sel(Multiplexador), .a(I8[4]), .b(I9[4]), .c(I10[4]), .d(I11[4]), .e(I12[4]), .f(I13[4]), .g(I14[4]),
    .h(II15[4]), .saida(multiplexador8entradas_13_saida));
  multiplexador8entradas multiplexador8entradas_14 (
    .sel(Multiplexador), .a(I8[5]), .b(I9[5]), .c(I10[5]), .d(I11[5]), .e(I12[5]), .f(I13[5]), .g(I14[5]),
    .h(II15[5]), .saida(multiplexador8entradas_14_saida));
  multiplexador8entradas multiplexador8entradas_15 (
    .sel(Multiplexador), .a(I8[6]), .b(I9[6]), .c(I10[6]), .d(I11[6]), .e(I12[6]), .f(I13[6]), .g(I14[6]),
    .h(II15[6]), .saida(multiplexador8entradas_15_saida));
  multiplexador8entradas multiplexador8entradas_16 (
    .sel(Multiplexador), .a(I8[7]), .b(I9[7]), .c(I10[7]), .d(I11[7]), .e(I12[7]), .f(I13[7]), .g(I14[7]),
    .h(II15[7]), .saida(multiplexador8entradas_16_saida));
endmodule

module shift2esq (
  input  [7:0] entrada,
  output [7:0] saida
);


  assign saida = {entrada[5:0], 2'b00};
endmodule

module shift2dir (
  input  [7:0] entrada,
  output [7:0] saida
);


  assign saida = {2'b00, entrada[7:2]};
endmodule
