// Logisim project 11.Extensordesinal.circ as structural Verilog: 4 circuits, main circuit main
module main (
  input  [3:0] in_1,
  output [7:0] out_2
);


  assign out_2 = {4'b0000, in_1};
endmodule

module srlatch (
  input  in_1,
  input  in_2,
  output out_3,
  output out_4
);

  nand nand_1 (out_3, in_1, out_4);
  nand nand_2 (out_4, out_3, in_2);
endmodule

module dflipflop (
  input  D,
  input  Clk,
  output Q,
  output Qb
);

  wire nand_1_out, nand_2_out, nand_3_out, nand_4_out, not_1_out, not_2_out, not_3_out, srlatch_1_out_3;

  not not_1 (not_1_out, D);
  nand nand_1 (nand_1_out, D, Clk);
  nand nand_2 (nand_2_out, Clk, not_1_out);
  not not_2 (not_2_out, Clk);
  srlatch srlatch_1 (.in_1(nand_1_out), .in_2(nand_2_out), .out_3(srlatch_1_out_3));  // open: out_4
  not not_3 (not_3_out, srlatch_1_out_3);
  nand nand_3 (nand_3_out, srlatch_1_out_3, not_2_out);
  nand nand_4 (nand_4_out, not_2_out, not_3_out);
  srlatch srlatch_2 (.in_1(nand_3_out), .in_2(nand_4_out), .out_3(Q), .out_4(Qb));
endmodule

module jkflipflop (
  input  J,
  input  K,
  input  Clk,
  output out_4,
  output out_5
);

  wire and_1_out, and_2_out, or_1_out;

  and and_1 (and_1_out, out_5, J);
  and and_2 (and_2_out, ~K, out_4);  // AND_Gate
  or or_1 (or_1_out, and_1_out, and_2_out);
  dflipflop dflipflop_1 (.D(or_1_out), .Clk(Clk), .Q(out_4), .Qb(out_5));
endmodule
