// Logisim project 14.DetectorParidadeImpar.circ as structural Verilog: 1 circuit, main circuit main
module main (
  input  [7:0] in_1,
  input  [7:0] in_2,
  output out_3,
  output out_4
);

  wire and_1_out, and_2_out, and_3_out, and_4_out, and_5_out, and_6_out, and_7_out, and_8_out, and_9_out,
       and_10_out, and_11_out, and_12_out, and_13_out, and_14_out, or_1_out, or_2_out, or_3_out, or_4_out,
       or_5_out, or_6_out, xor_1_out, xor_2_out, xor_3_out, xor_4_out, xor_5_out, xor_6_out;

  and and_1 (and_1_out, in_1[0], ~in_1[1]);  // AND_Gate
  and and_2 (and_2_out, ~in_1[0], in_1[1]);  // AND_Gate
  and and_3 (and_3_out, in_1[2], ~in_1[3]);  // AND_Gate
  and and_4 (and_4_out, ~in_1[2], in_1[3]);  // AND_Gate
  and and_5 (and_5_out, in_1[4], ~in_1[5]);  // AND_Gate
  and and_6 (and_6_out, ~in_1[4], in_1[5]);  // AND_Gate
  and and_7 (and_7_out, in_1[6], ~in_1[7]);  // AND_Gate
  and and_8 (and_8_out, ~in_1[6], in_1[7]);  // AND_Gate
  xor xor_1 (xor_1_out, in_2[0], in_2[1]);
  xor xor_2 (xor_2_out, in_2[2], in_2[3]);
  xor xor_3 (xor_3_out, in_2[4], in_2[5]);
  xor xor_4 (xor_4_out, in_2[6], in_2[7]);
  or or_1 (or_1_out, and_1_out, and_2_out);
  or or_2 (or_2_out, and_3_out, and_4_out);
  or or_3 (or_3_out, and_5_out, and_6_out);
  or or_4 (or_4_out, and_7_out, and_8_out);
  xor xor_5 (xor_5_out, xor_1_out, xor_2_out);
  xor xor_6 (xor_6_out, xor_3_out, xor_4_out);
  and and_9 (and_9_out, or_1_out, ~or_2_out);  // AND_Gate
  and and_10 (and_10_out, ~or_1_out, or_2_out);  // AND_Gate
  and and_11 (and_11_out, or_3_out, ~or_4_out);  // AND_Gate
  and and_12 (and_12_out, ~or_3_out, or_4_out);  // AND_Gate
  xor xor_7 (out_4, xor_5_out, xor_6_out);
  or or_5 (or_5_out, and_9_out, and_10_out);
  or or_6 (or_6_out, and_11_out, and_12_out);
  and and_13 (and_13_out, or_5_out, ~or_6_out);  // AND_Gate
  and and_14 (and_14_out, ~or_5_out, or_6_out);  // AND_Gate
  or or_7 (out_3, and_13_out, and_14_out);

  // Notes on the sheet:
  //   Detector de paridade impar usando XOR
  //   Detector de paridade impar com AND, NOT e OR
  //   Estamos adaptando a porta XOR= (A . não B) + (não A . B)
endmodule
