// Logisim project 15.CircuitoOtimizado.circ as structural Verilog: 1 circuit, main circuit main
module main (
  input  A,
  input  B,
  input  C,
  input  Ao,
  input  Bo,
  input  Co,
  output out_7,
  output out_8
);

  wire and_1_out, and_2_out, and_3_out, and_4_out, and_5_out, and_6_out, and_7_out, and_8_out, not_1_out,
       not_2_out, not_3_out, not_4_out, not_5_out, not_6_out;

  not not_1 (not_1_out, A);
  not not_2 (not_2_out, Ao);
  not not_3 (not_3_out, B);
  not not_4 (not_4_out, Bo);
  not not_5 (not_5_out, C);
  not not_6 (not_6_out, Co);
  and and_1 (and_1_out, not_1_out, not_3_out, C);
  and and_2 (and_2_out, not_1_out, B, C);
  and and_3 (and_3_out, A, not_3_out, not_5_out);
  and and_4 (and_4_out, A, not_3_out, C);
  and and_5 (and_5_out, A, B, not_5_out);
  and and_6 (and_6_out, not_2_out, Co);
  and and_7 (and_7_out, not_4_out, Co);
  and and_8 (and_8_out, Ao, not_6_out);
  or or_1 (out_8, and_6_out, and_7_out, and_8_out);
  or or_2 (out_7, and_1_out, and_2_out, and_3_out, and_4_out, and_5_out);

  // Notes on the sheet:
  //   dada a tabela verdade:
  //   A   B   C   ||S||
  //   0    0    0     0
  //   0    0    1     1
  //   0    1    0     0
  //   0    1    1     1
  //   1    0    0     1
  //   1    0    1     1
  //   1    1    0     1
  //   1    1    1     0
  //   Sem Otimização
  //   Com Otimização
endmodule
