// Logisim project 16.Display7Segmentos.circ as structural Verilog: 2 circuits, main circuit main
module main (
  input  [3:0] in_1
);

  wire bintohex_1_azinho, bintohex_1_bzinho, bintohex_1_czinho, bintohex_1_dzinho, bintohex_1_ezinho,
       bintohex_1_fzinho, bintohex_1_gzinho;

  BinToHex bintohex_1 (
    .D(in_1[3]), .C(in_1[2]), .B(in_1[1]), .A(in_1[0]), .azinho(bintohex_1_azinho),
    .bzinho(bintohex_1_bzinho), .czinho(bintohex_1_czinho), .dzinho(bintohex_1_dzinho),
    .ezinho(bintohex_1_ezinho), .fzinho(bintohex_1_fzinho), .gzinho(bintohex_1_gzinho));
  _7_Segment_Display u_7_segment_display_1 (
    .g(bintohex_1_gzinho), .f(bintohex_1_fzinho), .a(bintohex_1_azinho), .b(bintohex_1_bzinho),
    .e(bintohex_1_ezinho), .d(bintohex_1_dzinho), .c(bintohex_1_czinho));  // open: dp
endmodule

module BinToHex (
  input  D,
  input  C,
  input  B,
  input  A,
  output azinho,
  output bzinho,
  output czinho,
  output dzinho,
  output ezinho,
  output fzinho,
  output gzinho
);

  wire and_1_out, and_2_out, and_3_out, and_4_out, and_5_out, and_6_out, and_7_out, and_8_out, and_9_out,
       and_10_out, and_11_out, and_12_out, and_13_out, and_14_out, and_15_out, and_16_out, and_17_out,
       and_18_out, and_19_out, and_20_out, and_21_out, and_22_out, and_23_out, and_24_out, and_25_out,
       and_26_out, and_27_out, and_28_out, and_29_out, and_30_out, and_31_out, and_32_out, and_33_out,
       and_34_out, and_35_out, not_1_out, not_2_out, not_3_out, not_4_out;

  not not_1 (not_1_out, D);
  not not_2 (not_2_out, C);
  not not_3 (not_3_out, B);
  not not_4 (not_4_out, A);
  and and_1 (and_1_out, not_2_out, not_4_out);
  and and_2 (and_2_out, not_1_out, B);
  and and_3 (and_3_out, not_1_out, C, A);
  and and_4 (and_4_out, D, not_2_out, not_3_out);
  and and_5 (and_5_out, D, not_4_out);
  and and_6 (and_6_out, C, B);
  and and_7 (and_7_out, not_1_out, not_3_out, not_4_out);
  and and_8 (and_8_out, not_1_out, B, A);
  and and_9 (and_9_out, not_2_out, not_4_out);
  and and_10 (and_10_out, D, not_3_out, A);
  and and_11 (and_11_out, not_1_out, not_2_out);
  and and_12 (and_12_out, not_1_out, C);
  and and_13 (and_13_out, D, not_2_out);
  and and_14 (and_14_out, not_3_out, A);
  and and_15 (and_15_out, not_2_out, not_3_out);
  and and_16 (and_16_out, not_2_out, A);
  and and_17 (and_17_out, C, not_3_out, A);
  and and_18 (and_18_out, not_1_out, not_2_out, not_4_out);
  and and_19 (and_19_out, not_2_out, B, A);
  and and_20 (and_20_out, D, not_3_out);
  and and_21 (and_21_out, C, B, not_4_out);
  and and_22 (and_22_out, not_2_out, not_4_out);
  and and_23 (and_23_out, B, not_4_out);
  and and_24 (and_24_out, D, B);
  and and_25 (and_25_out, D, C);
  and and_26 (and_26_out, not_3_out, not_4_out);
  and and_27 (and_27_out, not_1_out, C, not_3_out);
  and and_28 (and_28_out, C, not_4_out);
  and and_29 (and_29_out, D, not_2_out);
  and and_30 (and_30_out, D, B);
  and and_31 (and_31_out, not_2_out, B);
  and and_32 (and_32_out, D, not_2_out);
  and and_33 (and_33_out, not_1_out, C, not_3_out);
  and and_34 (and_34_out, B, not_4_out);
  and and_35 (and_35_out, D, A);
  or or_1 (azinho, and_1_out, and_2_out, and_3_out, and_4_out, and_5_out, and_6_out);
  or or_2 (bzinho, and_7_out, and_8_out, and_9_out, and_10_out, and_11_out);
  or or_3 (czinho, and_12_out, and_13_out, and_14_out, and_15_out, and_16_out);
  or or_4 (dzinho, and_17_out, and_18_out, and_19_out, and_20_out, and_21_out);
  or or_5 (ezinho, and_22_out, and_23_out, and_24_out, and_25_out);
  or or_6 (fzinho, and_26_out, and_27_out, and_28_out, and_29_out, and_30_out);
  or or_7 (gzinho, and_31_out, and_32_out, and_33_out, and_34_out, and_35_out);
endmodule
