// Logisim project 17.NumeroPrimo.circ as structural Verilog: 3 circuits, main circuit main
module main (
  input  [3:0] in_1,
  input  [3:0] in_2,
  output out_3,
  output out_4
);

  PrimoComOtimizacao primocomotimizacao_1 (.A(in_1[3]), .B(in_1[2]), .C(in_1[1]), .D(in_1[0]), .out_5(out_3));
  PrimoSemOtimizacao primosemotimizacao_1 (.A(in_2[3]), .B(in_2[2]), .C(in_2[1]), .D(in_2[0]), .out_5(out_4));
endmodule

module PrimoSemOtimizacao (
  input  A,
  input  B,
  input  C,
  input  D,
  output out_5
);

  wire and_1_out, and_2_out, and_3_out, and_4_out, and_5_out, and_6_out, not_1_out, not_2_out, not_3_out,
       not_4_out;

  not not_1 (not_1_out, A);
  not not_2 (not_2_out, B);
  not not_3 (not_3_out, C);
  not not_4 (not_4_out, D);
  and and_1 (and_1_out, not_1_out, not_2_out, C, not_4_out);
  and and_2 (and_2_out, not_1_out, not_2_out, C, D);
  and and_3 (and_3_out, not_1_out, B, not_3_out, D);
  and and_4 (and_4_out, not_1_out, B, C, D);
  and and_5 (and_5_out, A, not_2_out, C, D);
  and and_6 (and_6_out, A, B, not_3_out, D);
  or or_1 (out_5, and_1_out, and_2_out, and_3_out, and_4_out, and_5_out, and_6_out);

  // Notes on the sheet:
  //   Esse circuito se baseia em uma tabela verdade onde se o Input for 2, 3, 5, 7, 11 ou 13. A saida exibirá "1" mostrando que o numero é primo
endmodule

module PrimoComOtimizacao (
  input  A,
  input  B,
  input  C,
  input  D,
  output out_5
);

  wire and_1_out, and_2_out, and_3_out, and_4_out, not_1_out, not_2_out, not_3_out, not_4_out;

  not not_1 (not_1_out, A);
  not not_2 (not_2_out, B);
  not not_3 (not_3_out, C);
  not not_4 (not_4_out, D);
  and and_1 (and_1_out, B, not_3_out, D);
  and and_2 (and_2_out, A, not_2_out, C, D);
  and and_3 (and_3_out, not_1_out, C, D);
  and and_4 (and_4_out, not_1_out, not_2_out, C);
  or or_1 (out_5, and_1_out, and_2_out, and_3_out, and_4_out);

  // Notes on the sheet:
  //   Com a redução da expressão da tabela verdade obtemos: (B.C'.D) + (A.B'.C.D) + (A'.C.D) + (A'.B'.C)
endmodule
