// Logisim project 2.MultiplexadorDe4Entradas.circ as structural Verilog: 1 circuit, main circuit main
module main (
  input  A,
  input  B,
  input  C,
  input  D,
  input  S1,
  input  S2,
  output Q
);

  wire and_1_out, and_2_out, and_3_out, and_4_out, not_1_out, not_2_out;

  not not_1 (not_1_out, S1);
  not not_2 (not_2_out, S2);
  and and_1 (and_1_out, A, S1, S2);
  and and_2 (and_2_out, B, not_1_out, S2);
  and and_3 (and_3_out, C, S1, not_2_out);
  and and_4 (and_4_out, D, not_1_out, not_2_out);
  or or_1 (Q, and_1_out, and_2_out, and_3_out, and_4_out);
endmodule
