// Logisim project 4.SomadorInteiro4.circ as structural Verilog: 4 circuits, main circuit main
module main (
  input  in_1,
  input  [7:0] in_2,
  output [7:0] out_3,
  output Overflow
);

  somador8bits somador8bits_1 (
    .in_4(1'b0), .in_6(in_2[1]), .in_8(1'b0), .in_10(in_2[2]), .in_12(1'b1), .in_14(in_2[3]), .in_16(1'b0),
    .in_2(in_2[0]), .in_1(in_1), .in_5(1'b0), .in_7(in_2[5]), .in_9(1'b0), .in_11(in_2[6]), .in_13(1'b0),
    .in_15(in_2[7]), .in_17(1'b0), .in_3(in_2[4]), .out_18(out_3[7]), .out_19(out_3[6]), .out_20(out_3[5]),
    .Resultado(out_3[4]), .out_22(out_3[3]), .out_23(out_3[2]), .out_24(out_3[1]), .out_25(out_3[0]),
    .Overflow(Overflow));
endmodule

module somador1bit (
  input  a0,
  input  a1,
  input  cin,
  output s,
  output cout
);

  wire and_1_out, and_2_out, and_3_out, xor_1_out;

  xor xor_1 (xor_1_out, a0, a1);
  and and_1 (and_1_out, a0, a1);
  and and_2 (and_2_out, a1, cin);
  and and_3 (and_3_out, a0, cin);
  xor xor_2 (s, xor_1_out, cin);
  or or_1 (cout, and_1_out, and_2_out, and_3_out);
endmodule

module somador4bits (
  input  carryin,
  input  in_2,
  input  in_3,
  input  in_4,
  input  in_5,
  input  in_6,
  input  in_7,
  input  in_8,
  input  in_9,
  output c3,
  output c2,
  output c1,
  output c0,
  output cout_Overflow_9503aa3a
);

  wire somador1bit_2_cout, somador1bit_3_cout, somador1bit_4_cout;

  somador1bit somador1bit_1 (.a1(in_6), .cin(somador1bit_2_cout), .a0(in_2), .s(c3), .cout(cout_Overflow_9503aa3a));
  somador1bit somador1bit_2 (.a1(in_7), .cin(somador1bit_3_cout), .a0(in_3), .s(c2), .cout(somador1bit_2_cout));
  somador1bit somador1bit_3 (.a1(in_8), .cin(somador1bit_4_cout), .a0(in_4), .s(c1), .cout(somador1bit_3_cout));
  somador1bit somador1bit_4 (.a1(in_9), .cin(carryin), .a0(in_5), .s(c0), .cout(somador1bit_4_cout));
endmodule

module somador8bits (
  input  in_1,
  input  in_2,
  input  in_3,
  input  in_4,
  input  in_5,
  input  in_6,
  input  in_7,
  input  in_8,
  input  in_9,
  input  in_10,
  input  in_11,
  input  in_12,
  input  in_13,
  input  in_14,
  input  in_15,
  input  in_16,
  input  in_17,
  output out_18,
  output out_19,
  output out_20,
  output Resultado,
  output out_22,
  output out_23,
  output out_24,
  output out_25,
  output Overflow
);

  wire somador4bits_1_cout_overflow_9503aa3a;

  somador4bits somador4bits_1 (
    .in_6(in_16), .in_2(in_14), .in_7(in_12), .in_3(in_10), .in_8(in_8), .in_4(in_6), .carryin(in_1),
    .in_9(in_4), .in_5(in_2), .cout_Overflow_9503aa3a(somador4bits_1_cout_overflow_9503aa3a), .c3(out_22),
    .c2(out_23), .c1(out_24), .c0(out_25));
  somador4bits somador4bits_2 (
    .in_6(in_17), .in_2(in_15), .in_7(in_13), .in_3(in_11), .in_8(in_9), .in_4(in_7),
    .carryin(somador4bits_1_cout_overflow_9503aa3a), .in_9(in_5), .in_5(in_3),
    .cout_Overflow_9503aa3a(Overflow), .c3(out_18), .c2(out_19), .c1(out_20), .c0(Resultado));
endmodule
