// Logisim project 5.MemoriaRom.circ as structural Verilog: 7 circuits, main circuit main
module main (
  input  [2:0] Address,
  output [7:0] LeituraRegistrador
);

  RegistradoresMemoria registradoresmemoria_1 (.Adress(Address), .RegLido(LeituraRegistrador));

  // Notes on the sheet:
  //   Endereços
  //   Registrador 0 (000)
  //   Registrador 1 (001)
  //   Registrador 2 (010)
  //   Registrador 3 (011)
  //   Registrador 4 (100)
  //   Registrador 5 (101)
  //   Registrador 6 (110)
  //   Registrador 7 (111)
endmodule

module srlatch (
  input  in_1,
  input  in_2,
  output out_3,
  output out_4
);

  nand nand_1 (out_3, in_1, out_4);
  nand nand_2 (out_4, out_3, in_2);
endmodule

module dflipflop (
  input  D,
  input  Clk,
  output Q,
  output Qb
);

  wire nand_1_out, nand_2_out, nand_3_out, nand_4_out, not_1_out, not_2_out, not_3_out, srlatch_1_out_3;

  not not_1 (not_1_out, D);
  nand nand_1 (nand_1_out, D, Clk);
  nand nand_2 (nand_2_out, Clk, not_1_out);
  not not_2 (not_2_out, Clk);
  srlatch srlatch_1 (.in_1(nand_1_out), .in_2(nand_2_out), .out_3(srlatch_1_out_3));  // open: out_4
  not not_3 (not_3_out, srlatch_1_out_3);
  nand nand_3 (nand_3_out, srlatch_1_out_3, not_2_out);
  nand nand_4 (nand_4_out, not_2_out, not_3_out);
  srlatch srlatch_2 (.in_1(nand_3_out), .in_2(nand_4_out), .out_3(Q), .out_4(Qb));
endmodule

module jkflipflop (
  input  J,
  input  K,
  input  Clk,
  output out_4,
  output out_5
);

  wire and_1_out, and_2_out, or_1_out;

  and and_1 (and_1_out, out_5, J);
  and and_2 (and_2_out, ~K, out_4);  // AND_Gate
  or or_1 (or_1_out, and_1_out, and_2_out);
  dflipflop dflipflop_1 (.Clk(Clk), .D(or_1_out), .Q(out_4), .Qb(out_5));
endmodule

module reg8bits (
  input  Clock,
  input  [7:0] Entrada,
  output [7:0] Saida
);

  dflipflop dflipflop_1 (.Clk(Clock), .D(Entrada[7]), .Q(Saida[7]));  // open: Qb
  dflipflop dflipflop_2 (.Clk(Clock), .D(Entrada[6]), .Q(Saida[6]));  // open: Qb
  dflipflop dflipflop_3 (.Clk(Clock), .D(Entrada[5]), .Q(Saida[5]));  // open: Qb
  dflipflop dflipflop_4 (.Clk(Clock), .D(Entrada[4]), .Q(Saida[4]));  // open: Qb
  dflipflop dflipflop_5 (.Clk(Clock), .D(Entrada[3]), .Q(Saida[3]));  // open: Qb
  dflipflop dflipflop_6 (.Clk(Clock), .D(Entrada[2]), .Q(Saida[2]));  // open: Qb
  dflipflop dflipflop_7 (.Clk(Clock), .D(Entrada[1]), .Q(Saida[1]));  // open: Qb
  dflipflop dflipflop_8 (.Clk(Clock), .D(Entrada[0]), .Q(Saida[0]));  // open: Qb
endmodule

module multiplexador8entradas (
  input  [2:0] sel,
  input  a,
  input  b,
  input  c,
  input  d,
  input  e,
  input  f,
  input  g,
  input  h,
  output saida
);

  wire and_1_out, and_2_out, and_3_out, and_4_out, and_5_out, and_6_out, and_7_out, and_8_out, not_1_out,
       not_2_out, not_3_out;

  not not_1 (not_1_out, sel[2]);
  not not_2 (not_2_out, sel[1]);
  not not_3 (not_3_out, sel[0]);
  and and_1 (and_1_out, a, not_1_out, not_2_out, not_3_out);
  and and_2 (and_2_out, b, not_1_out, not_2_out, sel[0]);
  and and_3 (and_3_out, c, not_1_out, sel[1], not_3_out);
  and and_4 (and_4_out, d, not_1_out, sel[1], sel[0]);
  and and_5 (and_5_out, e, sel[2], not_2_out, not_3_out);
  and and_6 (and_6_out, f, sel[2], not_2_out, sel[0]);
  and and_7 (and_7_out, g, sel[2], sel[1], not_3_out);
  and and_8 (and_8_out, h, sel[2], sel[1], sel[0]);
  or or_1 (saida, and_1_out, and_2_out, and_3_out, and_4_out, and_5_out, and_6_out, and_7_out, and_8_out);
endmodule

module RegistradoresMemoria (
  input  [2:0] Adress,
  output [7:0] RegLido
);

  multiplexador8entradas multiplexador8entradas_1 (
    .sel(Adress), .a(1'b0), .b(1'b1), .c(1'b0), .d(1'b1), .e(1'b0), .f(1'b1), .g(1'b1), .h(1'b0),
    .saida(RegLido[0]));
  multiplexador8entradas multiplexador8entradas_2 (
    .sel(Adress), .a(1'b1), .b(1'b0), .c(1'b0), .d(1'b1), .e(1'b0), .f(1'b1), .g(1'b1), .h(1'b0),
    .saida(RegLido[1]));
  multiplexador8entradas multiplexador8entradas_3 (
    .sel(Adress), .a(1'b0), .b(1'b1), .c(1'b0), .d(1'b1), .e(1'b1), .f(1'b0), .g(1'b0), .h(1'b1),
    .saida(RegLido[2]));
  multiplexador8entradas multiplexador8entradas_4 (
    .sel(Adress), .a(1'b1), .b(1'b0), .c(1'b1), .d(1'b0), .e(1'b1), .f(1'b1), .g(1'b0), .h(1'b1),
    .saida(RegLido[3]));
  multiplexador8entradas multiplexador8entradas_5 (
    .sel(Adress), .a(1'b0), .b(1'b1), .c(1'b0), .d(1'b1), .e(1'b1), .f(1'b1), .g(1'b0), .h(1'b0),
    .saida(RegLido[4]));
  multiplexador8entradas multiplexador8entradas_6 (
    .sel(Adress), .a(1'b1), .b(1'b0), .c(1'b0), .d(1'b1), .e(1'b0), .f(1'b0), .g(1'b1), .h(1'b0),
    .saida(RegLido[5]));
  multiplexador8entradas multiplexador8entradas_7 (
    .sel(Adress), .a(1'b0), .b(1'b1), .c(1'b0), .d(1'b1), .e(1'b0), .f(1'b1), .g(1'b1), .h(1'b1),
    .saida(RegLido[6]));
  multiplexador8entradas multiplexador8entradas_8 (
    .sel(Adress), .a(1'b1), .b(1'b0), .c(1'b1), .d(1'b0), .e(1'b1), .f(1'b1), .g(1'b0), .h(1'b1),
    .saida(RegLido[7]));

  // Notes on the sheet:
  //   registrador 0 (000)
  //   registrador 1 (001)
  //   registrador 2 (010)
  //   registrador 3 (011)
  //   registrador 4 (100)
  //   registrador 5 (101)
  //   registrador 6 (110)
  //   registrador 7 (111)
endmodule
