// Logisim project 6.MemoriaRam.circ as structural Verilog: 6 circuits, main circuit main
module main (
  input  [2:0] Adress,
  input  WriteEn,
  input  [7:0] DataIn,
  output [7:0] DataOut
);

  wire a000_out, a001_out, a010_out, a011_out, a100_out, a101_out, a110_out, a111_out, and_1_out, and_2_out,
       and_3_out, and_4_out, and_5_out, and_6_out, and_7_out, and_8_out, Clk_out, not_1_out, not_2_out,
       not_3_out, not_4_out, not_5_out, not_6_out, not_7_out, not_8_out, not_9_out, not_10_out, not_11_out,
       not_12_out;
  wire [7:0] reg8bits_1_saida, reg8bits_2_saida, reg8bits_3_saida, reg8bits_4_saida, reg8bits_5_saida,
       reg8bits_6_saida, reg8bits_7_saida, reg8bits_8_saida;

  not not_1 (not_1_out, Adress[1]);
  not not_2 (not_2_out, Adress[2]);
  not not_3 (not_3_out, Adress[0]);
  not not_4 (not_4_out, Adress[2]);
  not not_5 (not_5_out, Adress[1]);
  not not_6 (not_6_out, Adress[2]);
  not not_7 (not_7_out, Adress[0]);
  not not_8 (not_8_out, Adress[2]);
  not not_9 (not_9_out, Adress[1]);
  not not_10 (not_10_out, Adress[0]);
  not not_11 (not_11_out, Adress[1]);
  not not_12 (not_12_out, Adress[0]);
  Clock Clk (.out(Clk_out));
  and a000 (a000_out, not_1_out, not_2_out, not_3_out);
  and a001 (a001_out, not_4_out, not_5_out, Adress[0]);
  and a010 (a010_out, not_6_out, Adress[1], not_7_out);
  and a011 (a011_out, not_8_out, Adress[1], Adress[0]);
  and a100 (a100_out, Adress[2], not_9_out, not_10_out);
  and a101 (a101_out, Adress[2], not_11_out, Adress[0]);
  and a110 (a110_out, Adress[2], Adress[1], not_12_out);
  and a111 (a111_out, Adress[2], Adress[1], Adress[0]);
  and and_1 (and_1_out, Clk_out, a000_out, WriteEn);
  and and_2 (and_2_out, Clk_out, a001_out, WriteEn);
  and and_3 (and_3_out, Clk_out, a010_out, WriteEn);
  and and_4 (and_4_out, Clk_out, a011_out, WriteEn);
  and and_5 (and_5_out, Clk_out, a100_out, WriteEn);
  and and_6 (and_6_out, Clk_out, a101_out, WriteEn);
  and and_7 (and_7_out, Clk_out, a110_out, WriteEn);
  and and_8 (and_8_out, Clk_out, a111_out, WriteEn);
  reg8bits reg8bits_1 (.Clock(and_1_out), .Entrada(DataIn), .Saida(reg8bits_1_saida));
  reg8bits reg8bits_2 (.Clock(and_2_out), .Entrada(DataIn), .Saida(reg8bits_2_saida));
  reg8bits reg8bits_3 (.Clock(and_3_out), .Entrada(DataIn), .Saida(reg8bits_3_saida));
  reg8bits reg8bits_4 (.Clock(and_4_out), .Entrada(DataIn), .Saida(reg8bits_4_saida));
  reg8bits reg8bits_5 (.Clock(and_5_out), .Entrada(DataIn), .Saida(reg8bits_5_saida));
  reg8bits reg8bits_6 (.Clock(and_6_out), .Entrada(DataIn), .Saida(reg8bits_6_saida));
  reg8bits reg8bits_7 (.Clock(and_7_out), .Entrada(DataIn), .Saida(reg8bits_7_saida));
  reg8bits reg8bits_8 (.Clock(and_8_out), .Entrada(DataIn), .Saida(reg8bits_8_saida));
  multiplexador8ent8bit multiplexador8ent8bit_1 (
    .R7(reg8bits_8_saida), .R0(reg8bits_1_saida), .R1(reg8bits_2_saida), .R2(reg8bits_3_saida),
    .R3(reg8bits_4_saida), .R4(reg8bits_5_saida), .Adress(Adress), .R5(reg8bits_6_saida),
    .R6(reg8bits_7_saida), .RegLido(DataOut));
endmodule

module srlatch (
  input  in_1,
  input  in_2,
  output out_3,
  output out_4
);

  nand nand_1 (out_3, in_1, out_4);
  nand nand_2 (out_4, out_3, in_2);
endmodule

module dflipflop (
  input  D,
  input  Clk,
  output Q,
  output Qb
);

  wire nand_1_out, nand_2_out, nand_3_out, nand_4_out, not_1_out, not_2_out, not_3_out, srlatch_1_out_3;

  not not_1 (not_1_out, D);
  nand nand_1 (nand_1_out, D, Clk);
  nand nand_2 (nand_2_out, Clk, not_1_out);
  not not_2 (not_2_out, Clk);
  srlatch srlatch_1 (.in_1(nand_1_out), .in_2(nand_2_out), .out_3(srlatch_1_out_3));  // open: out_4
  not not_3 (not_3_out, srlatch_1_out_3);
  nand nand_3 (nand_3_out, srlatch_1_out_3, not_2_out);
  nand nand_4 (nand_4_out, not_2_out, not_3_out);
  srlatch srlatch_2 (.in_1(nand_3_out), .in_2(nand_4_out), .out_3(Q), .out_4(Qb));
endmodule

module reg8bits (
  input  Clock,
  input  [7:0] Entrada,
  output [7:0] Saida
);

  dflipflop dflipflop_1 (.Clk(Clock), .D(Entrada[7]), .Q(Saida[7]));  // open: Qb
  dflipflop dflipflop_2 (.Clk(Clock), .D(Entrada[6]), .Q(Saida[6]));  // open: Qb
  dflipflop dflipflop_3 (.Clk(Clock), .D(Entrada[5]), .Q(Saida[5]));  // open: Qb
  dflipflop dflipflop_4 (.Clk(Clock), .D(Entrada[4]), .Q(Saida[4]));  // open: Qb
  dflipflop dflipflop_5 (.Clk(Clock), .D(Entrada[3]), .Q(Saida[3]));  // open: Qb
  dflipflop dflipflop_6 (.Clk(Clock), .D(Entrada[2]), .Q(Saida[2]));  // open: Qb
  dflipflop dflipflop_7 (.Clk(Clock), .D(Entrada[1]), .Q(Saida[1]));  // open: Qb
  dflipflop dflipflop_8 (.Clk(Clock), .D(Entrada[0]), .Q(Saida[0]));  // open: Qb
endmodule

module multiplexador8entradas (
  input  [2:0] sel,
  input  a,
  input  b,
  input  c,
  input  d,
  input  e,
  input  f,
  input  g,
  input  h,
  output saida
);

  wire and_1_out, and_2_out, and_3_out, and_4_out, and_5_out, and_6_out, and_7_out, and_8_out, not_1_out,
       not_2_out, not_3_out;

  not not_1 (not_1_out, sel[2]);
  not not_2 (not_2_out, sel[1]);
  not not_3 (not_3_out, sel[0]);
  and and_1 (and_1_out, a, not_1_out, not_2_out, not_3_out);
  and and_2 (and_2_out, b, not_1_out, not_2_out, sel[0]);
  and and_3 (and_3_out, c, not_1_out, sel[1], not_3_out);
  and and_4 (and_4_out, d, not_1_out, sel[1], sel[0]);
  and and_5 (and_5_out, e, sel[2], not_2_out, not_3_out);
  and and_6 (and_6_out, f, sel[2], not_2_out, sel[0]);
  and and_7 (and_7_out, g, sel[2], sel[1], not_3_out);
  and and_8 (and_8_out, h, sel[2], sel[1], sel[0]);
  or or_1 (saida, and_1_out, and_2_out, and_3_out, and_4_out, and_5_out, and_6_out, and_7_out, and_8_out);
endmodule

module multiplexador8ent8bit (
  input  [2:0] Adress,
  input  [7:0] R0,
  input  [7:0] R1,
  input  [7:0] R2,
  input  [7:0] R3,
  input  [7:0] R4,
  input  [7:0] R5,
  input  [7:0] R6,
  input  [7:0] R7,
  output [7:0] RegLido
);

  multiplexador8entradas multiplexador8entradas_1 (
    .sel(Adress), .a(R0[0]), .b(R1[0]), .c(R2[0]), .d(R3[0]), .e(R4[0]), .f(R5[0]), .g(R6[0]), .h(R7[0]),
    .saida(RegLido[0]));
  multiplexador8entradas multiplexador8entradas_2 (
    .sel(Adress), .a(R0[1]), .b(R1[1]), .c(R2[1]), .d(R3[1]), .e(R4[1]), .f(R5[1]), .g(R6[1]), .h(R7[1]),
    .saida(RegLido[1]));
  multiplexador8entradas multiplexador8entradas_3 (
    .sel(Adress), .a(R0[2]), .b(R1[2]), .c(R2[2]), .d(R3[2]), .e(R4[2]), .f(R5[2]), .g(R6[2]), .h(R7[2]),
    .saida(RegLido[2]));
  multiplexador8entradas multiplexador8entradas_4 (
    .sel(Adress), .a(R0[3]), .b(R1[3]), .c(R2[3]), .d(R3[3]), .e(R4[3]), .f(R5[3]), .g(R6[3]), .h(R7[3]),
    .saida(RegLido[3]));
  multiplexador8entradas multiplexador8entradas_5 (
    .sel(Adress), .a(R0[4]), .b(R1[4]), .c(R2[4]), .d(R3[4]), .e(R4[4]), .f(R5[4]), .g(R6[4]), .h(R7[4]),
    .saida(RegLido[4]));
  multiplexador8entradas multiplexador8entradas_6 (
    .sel(Adress), .a(R0[5]), .b(R1[5]), .c(R2[5]), .d(R3[5]), .e(R4[5]), .f(R5[5]), .g(R6[5]), .h(R7[5]),
    .saida(RegLido[5]));
  multiplexador8entradas multiplexador8entradas_7 (
    .sel(Adress), .a(R0[6]), .b(R1[6]), .c(R2[6]), .d(R3[6]), .e(R4[6]), .f(R5[6]), .g(R6[6]), .h(R7[6]),
    .saida(RegLido[6]));
  multiplexador8entradas multiplexador8entradas_8 (
    .sel(Adress), .a(R0[7]), .b(R1[7]), .c(R2[7]), .d(R3[7]), .e(R4[7]), .f(R5[7]), .g(R6[7]), .h(R7[7]),
    .saida(RegLido[7]));
endmodule
