// Logisim project 7.Bancode4Registradores8bits.circ as structural Verilog: 8 circuits, main circuit main
module main (
  input  [1:0] in_1,
  input  in_2,
  input  [7:0] in_3,
  input  [7:0] in_4,
  input  [7:0] in_5,
  input  [7:0] in_6,
  output [7:0] out_7
);

  wire and_1_out, and_2_out, and_3_out, and_4_out, and_5_out, and_6_out, and_7_out, and_8_out, not_1_out,
       not_2_out, not_3_out, not_4_out;
  wire [7:0] reg8bits_1_saida, reg8bits_2_saida, reg8bits_3_saida, reg8bits_4_saida;

  not not_1 (not_1_out, in_1[1]);
  not not_2 (not_2_out, in_1[0]);
  not not_3 (not_3_out, in_1[0]);
  not not_4 (not_4_out, in_1[1]);
  and and_1 (and_1_out, not_1_out, not_2_out);
  and and_2 (and_2_out, in_1[1], not_3_out);
  and and_3 (and_3_out, not_4_out, in_1[0]);
  and and_4 (and_4_out, in_1[1], in_1[0]);
  and and_5 (and_5_out, in_2, and_1_out);
  and and_6 (and_6_out, in_2, and_2_out);
  and and_7 (and_7_out, in_2, and_3_out);
  and and_8 (and_8_out, in_2, and_4_out);
  reg8bits reg8bits_1 (.Clock(and_5_out), .Entrada(in_3), .Saida(reg8bits_1_saida));
  reg8bits reg8bits_2 (.Clock(and_6_out), .Entrada(in_4), .Saida(reg8bits_2_saida));
  reg8bits reg8bits_3 (.Clock(and_7_out), .Entrada(in_5), .Saida(reg8bits_3_saida));
  reg8bits reg8bits_4 (.Clock(and_8_out), .Entrada(in_6), .Saida(reg8bits_4_saida));
  multiplexador8bits multiplexador8bits_1 (
    .I1(reg8bits_1_saida), .I2(reg8bits_3_saida), .Sel(in_1), .I3(reg8bits_2_saida), .I4(reg8bits_4_saida),
    .s(out_7));
endmodule

module srlatch (
  input  in_1,
  input  in_2,
  output out_3,
  output out_4
);

  nand nand_1 (out_3, in_1, out_4);
  nand nand_2 (out_4, out_3, in_2);
endmodule

module dflipflop (
  input  D,
  input  Clk,
  output Q,
  output Qb
);

  wire nand_1_out, nand_2_out, nand_3_out, nand_4_out, not_1_out, not_2_out, not_3_out, srlatch_1_out_3;

  not not_1 (not_1_out, D);
  nand nand_1 (nand_1_out, D, Clk);
  nand nand_2 (nand_2_out, Clk, not_1_out);
  not not_2 (not_2_out, Clk);
  srlatch srlatch_1 (.in_1(nand_1_out), .in_2(nand_2_out), .out_3(srlatch_1_out_3));  // open: out_4
  not not_3 (not_3_out, srlatch_1_out_3);
  nand nand_3 (nand_3_out, srlatch_1_out_3, not_2_out);
  nand nand_4 (nand_4_out, not_2_out, not_3_out);
  srlatch srlatch_2 (.in_1(nand_3_out), .in_2(nand_4_out), .out_3(Q), .out_4(Qb));
endmodule

module jkflipflop (
  input  J,
  input  K,
  input  Clk,
  output out_4,
  output out_5
);

  wire and_1_out, and_2_out, or_1_out;

  and and_1 (and_1_out, out_5, J);
  and and_2 (and_2_out, ~K, out_4);  // AND_Gate
  or or_1 (or_1_out, and_1_out, and_2_out);
  dflipflop dflipflop_1 (.Clk(Clk), .D(or_1_out), .Q(out_4), .Qb(out_5));
endmodule

module reg8bits (
  input  Clock,
  input  [7:0] Entrada,
  output [7:0] Saida
);

  dflipflop dflipflop_1 (.Clk(Clock), .D(Entrada[7]), .Q(Saida[7]));  // open: Qb
  dflipflop dflipflop_2 (.Clk(Clock), .D(Entrada[6]), .Q(Saida[6]));  // open: Qb
  dflipflop dflipflop_3 (.Clk(Clock), .D(Entrada[5]), .Q(Saida[5]));  // open: Qb
  dflipflop dflipflop_4 (.Clk(Clock), .D(Entrada[4]), .Q(Saida[4]));  // open: Qb
  dflipflop dflipflop_5 (.Clk(Clock), .D(Entrada[3]), .Q(Saida[3]));  // open: Qb
  dflipflop dflipflop_6 (.Clk(Clock), .D(Entrada[2]), .Q(Saida[2]));  // open: Qb
  dflipflop dflipflop_7 (.Clk(Clock), .D(Entrada[1]), .Q(Saida[1]));  // open: Qb
  dflipflop dflipflop_8 (.Clk(Clock), .D(Entrada[0]), .Q(Saida[0]));  // open: Qb
endmodule

module multiplexador4entradas (
  input  a,
  input  b,
  input  c,
  input  d,
  input  [1:0] sel,
  output s
);

  wire and_1_out, and_2_out, and_3_out, and_4_out, not_1_out, not_2_out;

  not not_1 (not_1_out, sel[0]);
  not not_2 (not_2_out, sel[1]);
  and and_1 (and_1_out, a, sel[1], sel[0]);
  and and_2 (and_2_out, b, sel[1], not_1_out);
  and and_3 (and_3_out, c, not_2_out, sel[0]);
  and and_4 (and_4_out, d, not_1_out, not_2_out);
  or or_1 (s, and_1_out, and_2_out, and_3_out, and_4_out);
endmodule

module aaa (
  input  [7:0] in_1,
  input  [1:0] in_2,
  input  in_3,
  output [7:0] out_4
);

  wire and_1_out, and_2_out, and_3_out, and_4_out, and_5_out, and_6_out, and_7_out, and_8_out, not_1_out,
       not_2_out, not_3_out, not_4_out;
  wire [7:0] reg8bits_1_saida, reg8bits_2_saida, reg8bits_3_saida, reg8bits_4_saida;

  not not_1 (not_1_out, in_2[1]);
  not not_2 (not_2_out, in_2[0]);
  not not_3 (not_3_out, in_2[0]);
  not not_4 (not_4_out, in_2[1]);
  and and_1 (and_1_out, not_1_out, not_2_out);
  and and_2 (and_2_out, in_2[1], not_3_out);
  and and_3 (and_3_out, not_4_out, in_2[0]);
  and and_4 (and_4_out, in_2[1], in_2[0]);
  and and_5 (and_5_out, in_3, and_1_out);
  and and_6 (and_6_out, in_3, and_2_out);
  and and_7 (and_7_out, in_3, and_3_out);
  and and_8 (and_8_out, in_3, and_4_out);
  reg8bits reg8bits_1 (.Clock(and_5_out), .Entrada(in_1), .Saida(reg8bits_1_saida));
  reg8bits reg8bits_2 (.Clock(and_6_out), .Entrada(in_1), .Saida(reg8bits_2_saida));
  reg8bits reg8bits_3 (.Clock(and_7_out), .Entrada(in_1), .Saida(reg8bits_3_saida));
  reg8bits reg8bits_4 (.Clock(and_8_out), .Entrada(in_1), .Saida(reg8bits_4_saida));
  Multiplexer #(.select(2), .width(8)) multiplexer_1 (
    .in0(reg8bits_1_saida), .in1(reg8bits_2_saida), .in2(reg8bits_3_saida), .in3(reg8bits_4_saida),
    .out(out_4), .sel(in_2));
endmodule

module multiplexador8bits (
  input  [7:0] I1,
  input  [7:0] I2,
  input  [7:0] I3,
  input  [7:0] I4,
  input  [1:0] Sel,
  output [7:0] s
);

  multiplexador4entradas multiplexador4entradas_1 (.a(I4[0]), .b(I3[0]), .c(I2[0]), .d(I1[0]), .sel(Sel), .s(s[0]));
  multiplexador4entradas multiplexador4entradas_2 (.a(I4[1]), .b(I3[1]), .c(I2[1]), .d(I1[1]), .sel(Sel), .s(s[1]));
  multiplexador4entradas multiplexador4entradas_3 (.a(I4[2]), .b(I3[2]), .c(I2[2]), .d(I1[2]), .sel(Sel), .s(s[2]));
  multiplexador4entradas multiplexador4entradas_4 (.a(I4[3]), .b(I3[3]), .c(I2[3]), .d(I1[3]), .sel(Sel), .s(s[3]));
  multiplexador4entradas multiplexador4entradas_5 (.a(I4[4]), .b(I3[4]), .c(I2[4]), .d(I1[4]), .sel(Sel), .s(s[4]));
  multiplexador4entradas multiplexador4entradas_6 (.a(I4[5]), .b(I3[5]), .c(I2[5]), .d(I1[5]), .sel(Sel), .s(s[5]));
  multiplexador4entradas multiplexador4entradas_7 (.a(I4[6]), .b(I3[6]), .c(I2[6]), .d(I1[6]), .sel(Sel), .s(s[6]));
  multiplexador4entradas multiplexador4entradas_8 (.a(I4[7]), .b(I3[7]), .c(I2[7]), .d(I1[7]), .sel(Sel), .s(s[7]));
endmodule
